# Fritzing sketch toilite (saved by Fritzing 0.9.3b)
breadboards: 1

parts:
  U1 = attiny85 [package=dip]
  LED1 = RGB LED (com. cathode, rbg) [package="5 mm [THT]"]
  R1 = Photocell (LDR) [package=THT]
  S1 = Pushbutton [package="[THT]"]
  R2 = Resistor [tolerance=±5% resistance=150 package="0603 [SMD]"]
  R3 = Resistor [tolerance=±5% resistance=100 package="0603 [SMD]"]
  R4 = Resistor [tolerance=±5% resistance=100 package="0603 [SMD]"]
  R5 = TRIMPOT [package=3386u]
  Q1 = NPN-Transistor [package="TO92 [THT]"]
  PIR1 = PIR sensor
  R6 = Resistor [tolerance=±5% resistance=1k package=THT]
  VCC1 = 4 x AAA Battery Mount

nets:
  N1: U1.Pin_3, R2.Pin_1
  N2: U1.Pin_4, R1.pin_0, R5.CW, Q1.E, PIR1.GND, R6.Pin_0, VCC1.-
  N3: U1.Pin_5, R4.Pin_1
  N4: U1.Pin_6, R3.Pin_1
  N5: U1.Pin_7, S1.Pin_1, S1.Pin_2, R6.Pin_1
  N6: U1.Pin_8, S1.Pin_3, S1.Pin_4, R5.CCW, PIR1.SIG
  N7: LED1.red_anode, R2.Pin_0
  N8: LED1.common_cathode, Q1.C
  N9: LED1.blue_anode, R4.Pin_0
  N10: LED1.green_anode, R3.Pin_0
  N11: R1.pin_1, R5.WIPER, Q1.B
  N12: PIR1.VDD, VCC1.+
